// Logisim project CLASS04-C02.circ as structural Verilog: 1 circuit, main circuit main
module main (
  input  A,
  input  B,
  input  C
);

  wire A_nBC_out, AB_nC_out, ABC_out, nABC_out, not_1_out, not_2_out, not_3_out, or_1_out;

  not not_1 (not_1_out, A);
  not not_2 (not_2_out, B);
  not not_3 (not_3_out, C);
  and ABC (ABC_out, A, B, C);
  and nABC (nABC_out, not_1_out, B, C);
  and A_nBC (A_nBC_out, not_2_out, A, C);
  and AB_nC (AB_nC_out, not_3_out, B, A);
  or or_1 (or_1_out, ABC_out, nABC_out, A_nBC_out, AB_nC_out);
  LED Q (.in(or_1_out));
endmodule
