// Logisim project CLASS04-C03.circ as structural Verilog: 1 circuit, main circuit main
module main (
  input  A,
  input  B,
  input  C
);

  wire A_nB_nC_out, and_1_out, nA_B_C_out, not_1_out, not_2_out, not_3_out;

  not not_1 (not_1_out, A);
  not not_2 (not_2_out, B);
  not not_3 (not_3_out, C);
  or A_nB_nC (A_nB_nC_out, A, not_2_out, not_3_out);
  or nA_B_C (nA_B_C_out, not_1_out, B, C);
  and and_1 (and_1_out, A_nB_nC_out, nA_B_C_out);
  LED Q (.in(and_1_out));
endmodule
