// Logisim project CLASS04-C04.circ as structural Verilog: 1 circuit, main circuit main
module main (
  input  A,
  input  B,
  input  C
);

  wire A_B_C_out, A_nB_C_out, and_1_out, nA_B_C_out, not_1_out, not_2_out;

  not not_1 (not_1_out, A);
  not not_2 (not_2_out, B);
  or A_B_C (A_B_C_out, A, B, C);
  or A_nB_C (A_nB_C_out, A, not_2_out, C);
  or nA_B_C (nA_B_C_out, not_1_out, B, C);
  and and_1 (and_1_out, A_B_C_out, A_nB_C_out, nA_B_C_out);
  LED Q (.in(and_1_out));
endmodule
