// Logisim project CLASS04-C05.circ as structural Verilog: 1 circuit, main circuit main
module main (
  input  A,
  input  B,
  input  C
);

  wire A_nBC_out, AB_nC_out, ABC_out, nA_nBC_out, nABC_out, not_1_out, not_2_out, not_3_out, or_1_out;

  not not_1 (not_1_out, A);
  not not_2 (not_2_out, B);
  not not_3 (not_3_out, C);
  and nA_nBC (nA_nBC_out, not_1_out, not_2_out, C);
  and nABC (nABC_out, not_1_out, B, C);
  and A_nBC (A_nBC_out, A, not_2_out, C);
  and AB_nC (AB_nC_out, A, B, not_3_out);
  and ABC (ABC_out, A, B, C);
  or or_1 (or_1_out, nA_nBC_out, nABC_out, A_nBC_out, AB_nC_out, ABC_out);
  LED Q (.in(or_1_out));
endmodule
