// Logisim project CLASS04-C06.circ as structural Verilog: 1 circuit, main circuit main
module main (
  input  A,
  input  B,
  input  C
);

  wire AB_C_out, AB_out;

  and AB (AB_out, A, B);
  or AB_C (AB_C_out, AB_out, C);
  LED led_1 (.in(AB_C_out));
endmodule
