// Logisim project CLASS05-C01.circ as structural Verilog: 1 circuit, main circuit main
module main (
  input  A,
  input  B,
  input  C
);

  wire A___C_out, B_nA_out, C___nB_out, CA_nC_out, not_1_out, not_2_out, not_3_out, or_1_out;

  not not_1 (not_1_out, A);
  not not_2 (not_2_out, B);
  not not_3 (not_3_out, C);
  xnor A___C (A___C_out, A, C);
  and B_nA (B_nA_out, B, not_1_out);
  xor C___nB (C___nB_out, C, not_2_out);
  and CA_nC (CA_nC_out, C, not_1_out, not_3_out);
  or or_1 (or_1_out, A___C_out, B_nA_out, C___nB_out, CA_nC_out);
  LED Q (.in(or_1_out));
endmodule
