// Logisim project CLASS05-C02.circ as structural Verilog: 1 circuit, main circuit main
module main (
  input  A,
  input  B,
  input  C
);

  wire AB_2_out, AB_out, AC_2_out, AC_out, and_1_out, BC_out, not_1_out, or_1_out, or_2_out;

  and AB (AB_out, A, B);
  and AC (AC_out, A, C);
  and AB_2 (AB_2_out, A, B);
  and AC_2 (AC_2_out, A, C);
  and BC (BC_out, C, B);
  not not_1 (not_1_out, BC_out);
  or or_1 (or_1_out, AB_out, AC_out);
  or or_2 (or_2_out, AB_2_out, AC_2_out, BC_out);
  and and_1 (and_1_out, not_1_out, or_1_out);
  LED Q (.in(or_2_out));
  LED R (.in(and_1_out));
endmodule
