// Logisim project CLASS07-C01.circ as structural Verilog: 1 circuit, main circuit main
module main (
  input  A,
  input  B,
  input  C
);

  wire nAC_out, nBC_out, not_1_out, not_2_out, or_1_out;

  not not_1 (not_1_out, A);
  not not_2 (not_2_out, B);
  and nBC (nBC_out, not_2_out, C);
  and nAC (nAC_out, not_1_out, C);
  or or_1 (or_1_out, nBC_out, nAC_out);
  LED Q (.in(or_1_out));
endmodule
