// Logisim project CLASS07-QUIZZ.circ as structural Verilog: 1 circuit, main circuit main
module main (
  input  A,
  input  B,
  input  C
);

  wire A_nB_out, and_1_out, nAC_out, nB_nA_C_out, nB_nA_out, nB_nC_out, not_1_out, not_2_out, not_3_out,
       or_1_out;

  not not_1 (not_1_out, A);
  not not_2 (not_2_out, B);
  not not_3 (not_3_out, C);
  or nB_nA (nB_nA_out, not_2_out, not_1_out);
  and A_nB (A_nB_out, A, not_2_out);
  and nAC (nAC_out, not_1_out, C);
  and nB_nC (nB_nC_out, not_2_out, not_3_out);
  and nB_nA_C (nB_nA_C_out, C, nB_nA_out);
  or or_1 (or_1_out, A_nB_out, nAC_out, nB_nC_out);
  LED R (.in(nB_nA_C_out));
  and and_1 (and_1_out, or_1_out, C);
  LED Q (.in(and_1_out));
endmodule
