// Logisim project CLASS10-C01.circ as structural Verilog: 1 circuit, main circuit main
module main (
  input  A,
  input  B,
  input  C,
  input  D
);

  wire and_1_out, and_2_out, nand_1_out, nand_2_out, nand_3_out, nand_4_out, nand_5_out, nand_6_out,
       nand_7_out, or_1_out, or_2_out;

  and and_1 (and_1_out, A, B);
  or or_1 (or_1_out, B, C);
  and and_2 (and_2_out, C, D);
  nand nand_1 (nand_1_out, B, B);
  nand nand_2 (nand_2_out, C, C);
  nand nand_3 (nand_3_out, A, B);
  nand nand_4 (nand_4_out, nand_1_out, nand_2_out);
  nand nand_5 (nand_5_out, C, D);
  or or_2 (or_2_out, and_1_out, or_1_out, and_2_out);
  nand nand_6 (nand_6_out, nand_4_out, nand_4_out);
  LED Q (.in(or_2_out));
  LED R (.in(nand_7_out));
  nand nand_7 (nand_7_out, nand_3_out, nand_6_out, nand_5_out);
endmodule
