// Logisim project CLASS10-C02.circ as structural Verilog: 1 circuit, main circuit main
module main (
  input  A,
  input  B,
  input  C,
  input  D,
  output Q,
  output R
);

  wire and_1_out, and_2_out, nor_1_out, nor_2_out, nor_3_out, nor_4_out, nor_5_out, nor_6_out, nor_7_out,
       nor_8_out, or_1_out;

  and and_1 (and_1_out, A, B);
  and and_2 (and_2_out, B, C);
  or or_1 (or_1_out, B, D);
  nor nor_1 (nor_1_out, A, A);
  nor nor_2 (nor_2_out, B, B);
  nor nor_3 (nor_3_out, C, C);
  nor nor_4 (nor_4_out, nor_1_out, nor_2_out);
  nor nor_5 (nor_5_out, nor_2_out, nor_3_out);
  nor nor_6 (nor_6_out, nor_7_out, nor_7_out);
  nor nor_7 (nor_7_out, B, D);
  or or_2 (Q, and_1_out, and_2_out, or_1_out);
  nor nor_8 (nor_8_out, nor_4_out, nor_5_out, nor_6_out);
  nor nor_9 (R, nor_8_out, nor_8_out);
endmodule
