// Logisim project CLASS11-C01.circ as structural Verilog: 1 circuit, main circuit main
module main (
  input  A,
  input  B,
  input  C,
  input  A_2,
  input  B_2,
  input  C_2,
  output Q,
  output R,
  output S,
  output Q_2,
  output R_2,
  output S_2
);

  wire nand_1_out, nand_2_out, nand_3_out, nand_4_out, nor_1_out;

  nand nand_1 (nand_1_out, B, B);
  nand nand_2 (nand_2_out, C, C);
  nor nor_1 (nor_1_out, A_2, A_2);
  nand nand_3 (nand_3_out, A, nand_2_out);
  nand nand_4 (nand_4_out, A, nand_1_out);
  nor nor_2 (Q_2, nor_1_out, C_2);
  nor nor_3 (R_2, nor_1_out, B_2);
  nand nand_5 (Q, nand_3_out, nand_3_out);
  nand nand_6 (R, nand_4_out, nand_4_out);

  assign S = B;
  assign S_2 = B_2;
endmodule
