// Logisim project CLASS12-C01.circ as structural Verilog: 1 circuit, main circuit main
module main (
  input  A,
  input  B,
  input  A_2,
  input  Cin,
  input  B_2,
  input  A_3,
  input  B_3,
  input  A_4,
  input  B_4,
  output Q,
  output R,
  output S,
  output T,
  output Cout
);

  wire and_1_out, and_2_out, and_3_out, and_4_out, and_5_out, and_6_out, and_7_out, and_8_out, or_1_out,
       or_2_out, or_3_out, xor_1_out, xor_3_out, xor_5_out, xor_7_out;

  xor xor_1 (xor_1_out, A, B);
  xor xor_2 (Q, xor_1_out, Cin);
  and and_1 (and_1_out, Cin, xor_1_out);
  and and_2 (and_2_out, A, B);
  or or_1 (or_1_out, and_1_out, and_2_out);
  xor xor_3 (xor_3_out, A_2, B_2);
  xor xor_4 (R, xor_3_out, or_1_out);
  and and_3 (and_3_out, or_1_out, xor_3_out);
  and and_4 (and_4_out, A_2, B_2);
  or or_2 (or_2_out, and_3_out, and_4_out);
  xor xor_5 (xor_5_out, A_3, B_3);
  xor xor_6 (S, xor_5_out, or_2_out);
  and and_5 (and_5_out, or_2_out, xor_5_out);
  and and_6 (and_6_out, A_3, B_3);
  or or_3 (or_3_out, and_5_out, and_6_out);
  xor xor_7 (xor_7_out, A_4, B_4);
  xor xor_8 (T, xor_7_out, or_3_out);
  and and_7 (and_7_out, or_3_out, xor_7_out);
  and and_8 (and_8_out, A_4, B_4);
  or or_4 (Cout, and_7_out, and_8_out);
endmodule
