// Logisim project CLASS04-C01.circ as structural Verilog: 1 circuit, main circuit main
module main (
  input  in_1,
  input  in_2,
  input  in_3
);

  wire ABC_out, nAB_nC_out, not_1_out, not_2_out, or_1_out;

  not not_1 (not_1_out, in_1);
  not not_2 (not_2_out, in_3);
  and ABC (ABC_out, in_1, in_2, in_3);
  and nAB_nC (nAB_nC_out, not_1_out, in_2, not_2_out);
  or or_1 (or_1_out, ABC_out, nAB_nC_out);
  LED Q (.in(or_1_out));
endmodule
