// Logisim project CLASS06-C01.circ as structural Verilog: 1 circuit, main circuit main
module main (
  input  \Α ,
  input  \Β ,
  input  C
);

  wire A_nB_out, ABC_out, AC_out, nA_nB_nC_out, nB_nC_out, not_1_out, not_2_out, not_3_out, or_1_out,
       or_2_out;

  not not_1 (not_1_out, \Α );
  not not_2 (not_2_out, \Β );
  not not_3 (not_3_out, C);
  and A_nB (A_nB_out, \Α , not_2_out);
  and nA_nB_nC (nA_nB_nC_out, not_1_out, not_2_out, not_3_out);
  and ABC (ABC_out, \Α , C, \Β );
  and AC (AC_out, \Α , C);
  and nB_nC (nB_nC_out, not_2_out, not_3_out);
  or or_1 (or_1_out, A_nB_out, nA_nB_nC_out, ABC_out);
  or or_2 (or_2_out, AC_out, nB_nC_out);
  LED Q (.in(or_1_out));
  LED R (.in(or_2_out));
endmodule
