// Logisim project CLASS06-C02.circ as structural Verilog: 1 circuit, main circuit main
module main (
  input  A,
  input  B,
  input  C
);

  wire A_nB_nC_out, A_nBC_2_out, A_nBC_out, ABC_out, and_1_out, nA_nB_nC_out, nA_nBC_2_out, nA_nBC_out,
       nABC_out, not_1_out, not_2_out, not_3_out, or_1_out;

  not not_1 (not_1_out, A);
  not not_2 (not_2_out, B);
  not not_3 (not_3_out, C);
  and nA_nBC (nA_nBC_out, not_1_out, not_2_out, C);
  and nABC (nABC_out, not_1_out, B, C);
  and A_nB_nC (A_nB_nC_out, A, not_2_out, not_3_out);
  and A_nBC (A_nBC_out, A, not_2_out, C);
  or ABC (ABC_out, A, B, C);
  or A_nBC_2 (A_nBC_2_out, A, not_2_out, C);
  or nA_nBC_2 (nA_nBC_2_out, not_1_out, not_2_out, C);
  or nA_nB_nC (nA_nB_nC_out, not_1_out, not_2_out, not_3_out);
  or or_1 (or_1_out, nA_nBC_out, nABC_out, A_nB_nC_out, A_nBC_out);
  LED Q (.in(or_1_out));
  and and_1 (and_1_out, ABC_out, A_nBC_2_out, nA_nBC_2_out, nA_nB_nC_out);
  LED R (.in(and_1_out));
endmodule
