// Logisim project CLASS08-C01.circ as structural Verilog: 1 circuit, main circuit main
module main (
  input  A,
  input  B,
  input  C
);

  wire and_1_out, nA_nB_out, nB_nA_out, nC_nA_out, nC_nB_out, not_1_out, not_2_out, not_3_out, or_1_out,
       or_2_out;

  not not_1 (not_1_out, A);
  not not_2 (not_2_out, B);
  not not_3 (not_3_out, C);
  and nA_nB (nA_nB_out, not_1_out, not_2_out);
  or or_1 (or_1_out, nA_nB_out, not_3_out);
  or nC_nB (nC_nB_out, not_3_out, not_2_out);
  or nC_nA (nC_nA_out, not_3_out, not_1_out);
  and nB_nA (nB_nA_out, not_1_out, not_2_out);
  LED Q (.in(or_1_out));
  LED R (.in(and_1_out));
  and and_1 (and_1_out, nC_nB_out, nC_nA_out);
  LED Z (.in(or_2_out));
  or or_2 (or_2_out, nB_nA_out, not_3_out);
endmodule
