// Logisim project CLASS09-C01.circ as structural Verilog: 1 circuit, main circuit main
module main (
  input  A,
  input  B,
  input  C
);

  wire and_1_out, nand_1_out, nand_2_out, nand_3_out, or_1_out;

  and and_1 (and_1_out, A, B);
  nand nand_1 (nand_1_out, A, B);
  nand nand_2 (nand_2_out, C, C);
  nand nand_3 (nand_3_out, nand_1_out, nand_2_out);
  or or_1 (or_1_out, and_1_out, C);
  LED Q (.in(nand_3_out));
  LED R (.in(or_1_out));
endmodule
