// Logisim project CLASS09-C02.circ as structural Verilog: 1 circuit, main circuit main
module main (
  input  A,
  input  B,
  input  C,
  input  D
);

  wire and_1_out, and_2_out, nand_1_out, nand_2_out, nand_3_out, nand_4_out, nand_5_out, nand_6_out,
       nand_7_out, or_1_out, or_2_out;

  nand nand_1 (nand_1_out, A, A);
  nand nand_2 (nand_2_out, B, B);
  nand nand_3 (nand_3_out, nand_1_out, nand_2_out);
  or or_1 (or_1_out, A, B);
  and and_1 (and_1_out, C, D);
  nand nand_4 (nand_4_out, C, D);
  nand nand_5 (nand_5_out, D, D);
  and and_2 (and_2_out, or_1_out, and_1_out);
  nand nand_6 (nand_6_out, nand_3_out, nand_4_out);
  or or_2 (or_2_out, and_2_out, D);
  LED led_1 (.in(or_2_out));
  nand nand_7 (nand_7_out, nand_6_out, nand_5_out);
  LED led_2 (.in(nand_7_out));
endmodule
