// Logisim project CLASS09-C03.circ as structural Verilog: 1 circuit, main circuit main
module main (
  input  A,
  input  B,
  input  C
);

  wire and_1_out, nand_1_out, nand_2_out, nand_3_out, nand_4_out, nand_5_out, nand_6_out, nand_7_out,
       nand_8_out, nand_9_out, nand_10_out, nor_1_out, not_1_out, not_2_out, not_3_out, or_1_out, or_2_out;

  not not_1 (not_1_out, A);
  not not_2 (not_2_out, B);
  not not_3 (not_3_out, C);
  nand nand_1 (nand_1_out, B, B);
  nand nand_2 (nand_2_out, C, C);
  nand nand_3 (nand_3_out, A, C);
  nand nand_4 (nand_4_out, A, nand_1_out);
  nand nand_5 (nand_5_out, B, nand_2_out);
  nand nand_6 (nand_6_out, nand_3_out, nand_3_out);
  nand nand_7 (nand_7_out, nand_4_out, nand_4_out);
  nand nand_8 (nand_8_out, B, A, C);
  nand nand_9 (nand_9_out, A, C);
  or or_1 (or_1_out, not_1_out, B);
  nor nor_1 (nor_1_out, C, not_2_out);
  and and_1 (and_1_out, not_1_out, not_2_out, not_3_out);
  nand nand_10 (nand_10_out, nand_6_out, nand_7_out, nand_5_out, nand_8_out);
  or or_2 (or_2_out, nand_9_out, or_1_out, nor_1_out, and_1_out);
  LED Q (.in(nand_10_out));
  LED R (.in(or_2_out));
endmodule
