// Logisim project CLASS11-C02.circ as structural Verilog: 1 circuit, main circuit main
module main (
  input  A,
  input  B,
  input  C,
  input  D,
  output Q,
  output R,
  output S
);

  wire nand_1_out, nand_2_out, nand_3_out, nand_4_out, nand_5_out;

  nand nand_1 (nand_1_out, C, C);
  nand nand_2 (nand_2_out, A, A);
  nand nand_3 (nand_3_out, nand_1_out, D);
  nand nand_4 (nand_4_out, nand_2_out, nand_1_out);
  nand nand_5 (nand_5_out, B, nand_1_out);
  nand nand_6 (S, nand_3_out, nand_3_out);
  nand nand_7 (Q, nand_4_out, nand_4_out);
  nand nand_8 (R, nand_5_out, nand_5_out);
endmodule
