// Logisim project CLASS15-C01.circ as structural Verilog: 1 circuit, main circuit main
module main (
  output C,
  output B,
  output A
);

  wire and_1_out, clock_1_out, or_1_out, Prclr_out;

  Clock clock_1 (.out(clock_1_out));
  Button Prclr (.out(Prclr_out));
  J_K_Flip_Flop #(.trigger("falling")) j_k_ff_1 (
    .J(1'b1), .clk(clock_1_out), .K(1'b1), .Q(A), .preset(1'b0), .en(1'b1), .reset(or_1_out));  // open: Qn
  or or_1 (or_1_out, Prclr_out, and_1_out);
  J_K_Flip_Flop #(.trigger("falling")) j_k_ff_2 (
    .J(1'b1), .clk(A), .K(1'b1), .Q(B), .preset(1'b0), .en(1'b1), .reset(or_1_out));  // open: Qn
  J_K_Flip_Flop #(.trigger("falling")) j_k_ff_3 (
    .J(1'b1), .clk(B), .K(1'b1), .Q(C), .preset(1'b0), .en(1'b1), .reset(or_1_out));  // open: Qn
  and and_1 (and_1_out, C, B);
endmodule
