// Logisim project CLASS15-HW.circ as structural Verilog: 1 circuit, main circuit main
module main (
  output C,
  output B,
  output A,
  output D,
  output out_5,
  output D_2,
  output C_2,
  output B_2,
  output A_2,
  output D_3,
  output C_3,
  output B_3,
  output A_3
);

  wire clock_1_out, Prclr_out, shift_register_1_out;

  Clock clock_1 (.out(clock_1_out));
  Button Prclr (.out(Prclr_out));
  J_K_Flip_Flop #(.trigger("falling")) j_k_ff_1 (
    .J(1'b1), .clk(clock_1_out), .K(1'b1), .Q(A), .preset(1'b0), .en(1'b1), .reset(Prclr_out));  // open: Qn
  J_K_Flip_Flop #(.trigger("falling")) j_k_ff_2 (
    .J(1'b1), .clk(A), .K(1'b1), .Q(B), .preset(1'b0), .en(1'b1), .reset(Prclr_out));  // open: Qn
  Shift_Register #(.length(4)) shift_register_1 (
    .shift(1'b1), .in(1'b1), .clk(clock_1_out), .out(shift_register_1_out), .load(1'b0), .clr(Prclr_out),
    .d0(A), .q0(D_2), .d1(B), .q1(C_2), .d2(C), .q2(B_2), .d3(D), .q3(A_2));
  J_K_Flip_Flop #(.trigger("falling")) j_k_ff_3 (
    .J(1'b1), .clk(B), .K(1'b1), .Q(C), .preset(1'b0), .en(1'b1), .reset(Prclr_out));  // open: Qn
  Shift_Register #(.length(4)) shift_register_2 (
    .shift(1'b1), .in(shift_register_1_out), .clk(clock_1_out), .out(out_5), .load(1'b0), .clr(Prclr_out),
    .d0(A), .q0(D_3), .d1(B), .q1(C_3), .d2(C), .q2(B_3), .d3(D), .q3(A_3));
  J_K_Flip_Flop #(.trigger("falling")) j_k_ff_4 (
    .J(1'b1), .clk(C), .K(1'b1), .Q(D), .preset(1'b0), .en(1'b1), .reset(Prclr_out));  // open: Qn
endmodule
