// Logisim project CLASS18-C01.circ as structural Verilog: 1 circuit, main circuit main
module main (
  output Q3,
  output Q2,
  output Q1
);

  wire and_1_out, and_2_out, and_3_out, and_4_out, Clock_out, not_1_out, not_2_out, not_3_out, or_1_out,
       or_2_out, or_3_out, Reset_out;

  Clock Clock (.out(Clock_out));
  Button Reset (.out(Reset_out));
  or or_1 (or_1_out, and_1_out, and_2_out);
  or or_2 (or_2_out, and_3_out, and_4_out);
  or or_3 (or_3_out, Q2, not_3_out);
  and and_1 (and_1_out, not_3_out, Q1);
  and and_2 (and_2_out, Q3, not_1_out);
  not not_1 (not_1_out, Q1);
  and and_3 (and_3_out, not_2_out, not_1_out);
  and and_4 (and_4_out, Q2, Q1);
  J_K_Flip_Flop u_Q1 (.J(or_3_out), .clk(Clock_out), .K(or_3_out), .Q(Q1), .reset(Reset_out));  // open: Qn, preset, en
  not not_2 (not_2_out, Q2);
  J_K_Flip_Flop u_Q2 (.J(not_3_out), .clk(Clock_out), .K(or_1_out), .Q(Q2), .reset(Reset_out));  // open: Qn, preset, en
  not not_3 (not_3_out, Q3);
  J_K_Flip_Flop u_Q3 (.J(or_2_out), .clk(Clock_out), .K(not_2_out), .Q(Q3), .reset(Reset_out));  // open: Qn, preset, en
endmodule
