// Logisim project SECTION2-NAND.circ as structural Verilog: 1 circuit, main circuit main
module main (
  input  A,
  input  B,
  input  C,
  output A_2,
  output B_2,
  output C_2
);

  wire nand_1_out, nand_2_out, nand_3_out, nand_4_out, nand_5_out, nand_6_out;

  nand nand_1 (nand_1_out, A, A);
  nand nand_2 (nand_2_out, B, B);
  nand nand_3 (nand_3_out, C, C);
  nand nand_4 (nand_4_out, nand_1_out, nand_3_out);
  nand nand_5 (nand_5_out, A, nand_2_out);
  nand nand_6 (nand_6_out, nand_2_out, C);
  nand nand_7 (A_2, nand_4_out, nand_4_out);
  nand nand_8 (B_2, nand_5_out, nand_6_out);
  nand nand_9 (C_2, nand_6_out, nand_6_out);
endmodule
