// Logisim project SECTION2.circ as structural Verilog: 1 circuit, main circuit main
module main (
  input  A,
  input  B,
  input  C,
  output A_2,
  output B_2,
  output C_2
);

  wire A_nB_out, not_1_out, not_2_out, not_3_out;

  not not_1 (not_1_out, A);
  not not_2 (not_2_out, B);
  not not_3 (not_3_out, C);
  and nA_nC (A_2, not_1_out, not_3_out);
  and A_nB (A_nB_out, A, not_2_out);
  and nBC (C_2, not_2_out, C);
  or or_1 (B_2, A_nB_out, C_2);
endmodule
