// Logisim project SECTION3.circ as structural Verilog: 1 circuit, main circuit main
module main (
  output Q3,
  output Q2,
  output Q1
);

  wire clock_1_out, not_1_out, not_2_out, not_3_out, nQ2Q1_out, nQ3_Q1_out, Q2_nQ1_out, Q3_nQ1_out, Q3Q2_out,
       RESET_out;

  Clock clock_1 (.out(clock_1_out));
  Button RESET (.out(RESET_out));
  and Q2_nQ1 (Q2_nQ1_out, not_1_out, Q2);
  and nQ2Q1 (nQ2Q1_out, not_2_out, Q1);
  or Q3_nQ1 (Q3_nQ1_out, Q3, not_1_out);
  or nQ3_Q1 (nQ3_Q1_out, not_3_out, Q1);
  and Q3Q2 (Q3Q2_out, Q3, Q2);
  J_K_Flip_Flop u_Q1 (
    .J(Q3Q2_out), .clk(clock_1_out), .K(1'b0), .Q(Q1), .preset(1'b0), .en(1'b1), .reset(RESET_out));  // open: Qn
  not not_1 (not_1_out, Q1);
  not not_2 (not_2_out, Q2);
  J_K_Flip_Flop u_Q2 (
    .J(Q3_nQ1_out), .clk(clock_1_out), .K(nQ3_Q1_out), .Q(Q2), .preset(1'b0), .en(1'b1), .reset(RESET_out));  // open: Qn
  J_K_Flip_Flop u_Q3 (
    .J(Q2_nQ1_out), .clk(clock_1_out), .K(nQ2Q1_out), .Q(Q3), .preset(1'b0), .en(1'b1), .reset(RESET_out));  // open: Qn
  not not_3 (not_3_out, Q3);
endmodule
