// Logisim project MIDTERM-2ALT.circ as structural Verilog: 1 circuit, main circuit main
module main (
  input  A,
  input  B,
  input  C,
  input  A_2,
  input  B_2,
  input  C_2,
  output Q,
  output Q_2
);

  wire n_nA_nB_out, n_nBC_out, nA_nB_out, nand_1_out, nand_2_out, nBC_out, not_1_out, not_2_out;

  not not_1 (not_1_out, A);
  not not_2 (not_2_out, B);
  nand nand_1 (nand_1_out, A_2, A_2);
  nand nand_2 (nand_2_out, B_2, B_2);
  and nA_nB (nA_nB_out, not_1_out, not_2_out);
  and nBC (nBC_out, not_2_out, C);
  nand n_nA_nB (n_nA_nB_out, nand_1_out, nand_2_out);
  nand n_nBC (n_nBC_out, nand_2_out, C_2);
  or or_1 (Q, nA_nB_out, nBC_out);
  nand nand_3 (Q_2, n_nA_nB_out, n_nBC_out);
endmodule
