// Logisim project MIDTERM-3.2.circ as structural Verilog: 1 circuit, main circuit main
module main (
  input  A,
  input  B,
  input  C,
  output out_4
);

  wire A_nBC_out, nA_nBC_out, nAB_nC_out, nABC_out, not_1_out, not_2_out, not_3_out;

  not not_1 (not_1_out, A);
  not not_2 (not_2_out, B);
  not not_3 (not_3_out, C);
  and nA_nBC (nA_nBC_out, not_1_out, not_2_out, C);
  and nAB_nC (nAB_nC_out, not_1_out, B, not_3_out);
  and nABC (nABC_out, not_1_out, B, C);
  and A_nBC (A_nBC_out, A, not_2_out, C);
  or or_1 (out_4, nA_nBC_out, nAB_nC_out, nABC_out, A_nBC_out);
endmodule
