// Logisim project MIDTERM-3.4.circ as structural Verilog: 1 circuit, main circuit main
module main (
  input  A,
  input  B,
  input  C,
  output Q
);

  wire nAB_out, nAC_out, nBC_out, not_1_out, not_2_out;

  not not_1 (not_1_out, A);
  not not_2 (not_2_out, B);
  and nBC (nBC_out, not_2_out, C);
  and nAC (nAC_out, not_1_out, C);
  and nAB (nAB_out, not_1_out, B);
  or or_1 (Q, nBC_out, nAC_out, nAB_out);
endmodule
