// Logisim project MIDTERM-3.5.circ as structural Verilog: 1 circuit, main circuit main
module main (
  input  A,
  input  B,
  input  C,
  output out_4
);

  wire n_nAB_out, n_nAC_out, n_nBC_out, nand_1_out, nand_2_out;

  nand nand_1 (nand_1_out, B, B);
  nand nand_2 (nand_2_out, A, A);
  nand n_nBC (n_nBC_out, nand_1_out, C);
  nand n_nAC (n_nAC_out, nand_2_out, C);
  nand n_nAB (n_nAB_out, nand_2_out, B);
  nand nand_3 (out_4, n_nBC_out, n_nAC_out, n_nAB_out);
endmodule
