// Logisim project PROJECT-DISPLAY.circ as structural Verilog: 1 circuit, main circuit main
module main (
  input  A,
  input  B,
  input  C,
  input  D,
  input  E,
  output out_6,
  output out_7,
  output out_8,
  output out_9,
  output out_10,
  output out_11,
  output out_12,
  output out_13,
  output out_14,
  output out_15,
  output out_16,
  output out_17,
  output out_18,
  output out_19,
  output out_20,
  output out_21
);

  wire A_nE_out, AB_out, AC_out, and_1_out, and_2_out, and_3_out, and_4_out, B_nC_nD_2_out, B_nC_nD_out,
       B_nC_out, B_nCD_out, B_nD_out, BC_2_out, BC_out, BD_2_out, BD_out, C_nD_nE_out, C_nD_out, CD_nE_out,
       CD_out, CDE_out, CLEAR_out, CLOCK_out, controlled_buffer_1_out, controlled_buffer_3_out,
       controlled_buffer_5_out, controlled_buffer_7_out, controlled_buffer_9_out, d_ff_1_q, nand_1_out,
       nand_2_out, nand_3_out, nand_4_out, nand_5_out, nand_9_out, nB_nD_out, nBC_nE_out, nBC_out, nBCE_out,
       nBD_nE_out, nBDE_out, nC_nD_out, nC_nDE_out, nDE_out, nor_1_out, nor_2_out, not_1_out, not_2_out,
       not_3_out, or_1_out, or_2_out, or_3_out, or_4_out, or_5_out, or_6_out, or_7_out, or_8_out, or_9_out,
       or_10_out, or_11_out;
  wire [1:0] counter_1_q;
  wire [3:0] controlled_buffer_2_out, controlled_buffer_4_out, controlled_buffer_6_out,
       controlled_buffer_8_out, nand_6_out;

  assign controlled_buffer_1_out = nor_1_out ? E : 1'bz;  // Controlled_Buffer controlled_buffer_1
  or or_1 (or_1_out, A, BD_out, C, nB_nD_out);
  and BD (BD_out, B, D);
  nand nand_1 (nand_1_out, B, B);
  nand nand_2 (nand_2_out, C, C);
  nand nand_3 (nand_3_out, D, D);
  or or_2 (or_2_out, nand_1_out, nC_nD_out, CD_out);
  and nB_nD (nB_nD_out, nand_1_out, nand_3_out);
  and nC_nD (nC_nD_out, nand_2_out, nand_3_out);
  D_Flip_Flop d_ff_1 (
    .clk(CLOCK_out), .D(controlled_buffer_1_out), .Q(d_ff_1_q), .preset(1'b0), .en(1'b1), .reset(1'b0));  // open: Qn
  or or_3 (or_3_out, B, nand_2_out, D);
  and CD (CD_out, C, D);
  nand nand_4 (nand_4_out, d_ff_1_q, d_ff_1_q);
  nor nor_1 (nor_1_out, counter_1_q[0], counter_1_q[1]);
  _7_Segment_Display u_7_segment_display_1 (
    .g(or_7_out), .f(or_6_out), .a(or_1_out), .b(or_2_out), .e(or_5_out), .d(or_4_out), .c(or_3_out));  // open: dp
  or or_4 (or_4_out, nB_nD_out, C_nD_out, B_nCD_out, nBC_out, A);
  and C_nD (C_nD_out, C, nand_3_out);
  and B_nCD (B_nCD_out, B, nand_2_out, D);
  nand BC (BC_out, B, C);
  nand BD_2 (BD_2_out, B, D);
  or or_5 (or_5_out, nB_nD_out, C_nD_out);
  and nBC (nBC_out, nand_1_out, C);
  nand CD_nE (CD_nE_out, C, D, nand_4_out);
  nand nBDE (nBDE_out, nand_1_out, D, d_ff_1_q);
  nand nBCE (nBCE_out, nand_1_out, C, d_ff_1_q);
  nand B_nC_nD (B_nC_nD_out, B, nand_2_out, nand_3_out);
  or or_6 (or_6_out, A, nC_nD_out, BC_2_out, B_nC_out, B_nD_out);
  and B_nC (B_nC_out, B, nand_2_out);
  and B_nD (B_nD_out, B, D);
  or or_7 (or_7_out, A, B_nC_out, nBC_out, C_nD_out);
  and BC_2 (BC_2_out, B, C);
  nand nand_5 (nand_5_out, A, A);
  nand A_nE (A_nE_out, A, nand_4_out);
  nand nand_6 (nand_6_out[0], nand_5_out, BC_out, BD_2_out);
  nand B_nC_nD_2 (B_nC_nD_2_out, B, nand_2_out, nand_3_out);
  nand C_nD_nE (C_nD_nE_out, C, nand_3_out, nand_4_out);
  nand nC_nDE (nC_nDE_out, nand_2_out, nand_3_out, d_ff_1_q);
  nand CDE (CDE_out, C, D, d_ff_1_q);
  nand nand_7 (nand_6_out[1], A_nE_out, CD_nE_out, nBDE_out, nBCE_out, B_nC_nD_out);
  nand nand_8 (nand_6_out[2], A_nE_out, B_nC_nD_2_out, C_nD_nE_out, nC_nDE_out, CDE_out);
  nand nDE (nDE_out, nand_3_out, d_ff_1_q);
  nand nBD_nE (nBD_nE_out, nand_1_out, D, nand_4_out);
  nand nBC_nE (nBC_nE_out, nand_1_out, C, nand_4_out);
  nand AB (AB_out, A, B);
  nand AC (AC_out, A, C);
  nand nand_9 (nand_9_out, AB_out, AC_out);
  nand nand_10 (nand_6_out[3], B_nC_nD_2_out, nDE_out, nBD_nE_out, nBC_nE_out);
  Button CLOCK (.out(CLOCK_out));
  Button CLEAR (.out(CLEAR_out));
  LED ERROR (.in(nand_9_out));
  assign controlled_buffer_2_out = and_2_out ? nand_6_out : 4'bz;  // Controlled_Buffer controlled_buffer_2
  and and_1 (and_1_out, CLOCK_out, not_1_out);
  not not_1 (not_1_out, nand_9_out);
  Register #(.width(4)) register_1 (
    .D(controlled_buffer_2_out), .en(1'b1), .Q({out_21, out_20, out_19, out_18}), .clk(CLOCK_out),
    .clr(or_8_out));
  or or_8 (or_8_out, controlled_buffer_3_out, CLEAR_out);
  assign controlled_buffer_3_out = and_2_out ? nand_9_out : 1'bz;  // Controlled_Buffer controlled_buffer_3
  and and_2 (and_2_out, counter_1_q[0], counter_1_q[1]);
  Counter #(.width(2), .max('h3), .ongoal("stay")) counter_1 (
    .count(1'b1), .Q(counter_1_q), .clk(and_1_out), .clr(CLEAR_out));  // open: load, D, carry
  assign controlled_buffer_4_out = and_3_out ? nand_6_out : 4'bz;  // Controlled_Buffer controlled_buffer_4
  Register #(.width(4)) register_2 (
    .D(controlled_buffer_4_out), .en(1'b1), .Q({out_17, out_16, out_15, out_14}), .clk(CLOCK_out),
    .clr(or_9_out));
  or or_9 (or_9_out, controlled_buffer_5_out, CLEAR_out);
  assign controlled_buffer_5_out = and_3_out ? nand_9_out : 1'bz;  // Controlled_Buffer controlled_buffer_5
  and and_3 (and_3_out, not_2_out, counter_1_q[1]);
  not not_2 (not_2_out, counter_1_q[0]);
  assign controlled_buffer_6_out = and_4_out ? nand_6_out : 4'bz;  // Controlled_Buffer controlled_buffer_6
  Register #(.width(4)) register_3 (
    .D(controlled_buffer_6_out), .en(1'b1), .Q({out_13, out_12, out_11, out_10}), .clk(CLOCK_out),
    .clr(or_10_out));
  or or_10 (or_10_out, controlled_buffer_7_out, CLEAR_out);
  assign controlled_buffer_7_out = and_4_out ? nand_9_out : 1'bz;  // Controlled_Buffer controlled_buffer_7
  and and_4 (and_4_out, counter_1_q[0], not_3_out);
  not not_3 (not_3_out, counter_1_q[1]);
  assign controlled_buffer_8_out = nor_2_out ? nand_6_out : 4'bz;  // Controlled_Buffer controlled_buffer_8
  Register #(.width(4)) register_4 (
    .D(controlled_buffer_8_out), .en(1'b1), .Q({out_9, out_8, out_7, out_6}), .clk(CLOCK_out), .clr(or_11_out));
  or or_11 (or_11_out, controlled_buffer_9_out, CLEAR_out);
  assign controlled_buffer_9_out = nor_2_out ? nand_9_out : 1'bz;  // Controlled_Buffer controlled_buffer_9
  nor nor_2 (nor_2_out, counter_1_q[0], counter_1_q[1]);
endmodule
