// Logisim project PROJECT-NAND.circ as structural Verilog: 1 circuit, main circuit main
module main (
  input  A,
  input  B,
  input  C,
  input  D,
  input  E,
  output Af,
  output Bf,
  output Cf,
  output Df
);

  wire A_nE_out, AB_out, AC_out, B_nC_nD_2_out, B_nC_nD_out, BC_out, BD_out, C_nD_nE_out, CD_nE_out, CDE_out,
       nand_1_out, nand_2_out, nand_3_out, nand_4_out, nand_5_out, nand_10_out, nBC_nE_out, nBCE_out,
       nBD_nE_out, nBDE_out, nC_nDE_out, nDE_out;

  nand nand_1 (nand_1_out, B, B);
  nand nand_2 (nand_2_out, C, C);
  nand nand_3 (nand_3_out, D, D);
  nand nand_4 (nand_4_out, E, E);
  nand BC (BC_out, B, C);
  nand BD (BD_out, B, D);
  nand CD_nE (CD_nE_out, C, D, nand_4_out);
  nand nBDE (nBDE_out, nand_1_out, D, E);
  nand nBCE (nBCE_out, nand_1_out, C, E);
  nand B_nC_nD (B_nC_nD_out, B, nand_2_out, nand_3_out);
  nand nand_5 (nand_5_out, A, A);
  nand A_nE (A_nE_out, A, nand_4_out);
  nand nand_6 (Af, nand_5_out, BC_out, BD_out);
  nand nand_7 (Bf, A_nE_out, CD_nE_out, nBDE_out, nBCE_out, B_nC_nD_out);
  nand B_nC_nD_2 (B_nC_nD_2_out, B, nand_2_out, nand_3_out);
  nand C_nD_nE (C_nD_nE_out, C, nand_3_out, nand_4_out);
  nand nC_nDE (nC_nDE_out, nand_2_out, nand_3_out, E);
  nand CDE (CDE_out, C, D, E);
  nand nand_8 (Cf, A_nE_out, B_nC_nD_2_out, C_nD_nE_out, nC_nDE_out, CDE_out);
  nand nDE (nDE_out, nand_3_out, E);
  nand nBD_nE (nBD_nE_out, nand_1_out, D, nand_4_out);
  nand nBC_nE (nBC_nE_out, nand_1_out, C, nand_4_out);
  nand AB (AB_out, A, B);
  nand AC (AC_out, A, C);
  nand nand_9 (Df, B_nC_nD_2_out, nDE_out, nBD_nE_out, nBC_nE_out);
  nand nand_10 (nand_10_out, AB_out, AC_out);
  LED ERROR (.in(nand_10_out));
endmodule
