// Logisim project PROJECT.circ as structural Verilog: 1 circuit, main circuit main
module main (
  input  A,
  input  B,
  input  C,
  input  D,
  input  E,
  output Af,
  output Bf,
  output Cf,
  output Df
);

  wire A_nE_out, AB_out, AC_out, B_nC_nD_2_out, B_nC_nD_out, BC_out, BD_out, C_nD_nE_out, CD_nE_out, CDE_out,
       nBC_nE_out, nBCE_out, nBD_nE_out, nBDE_out, nC_nDE_out, nDE_out, not_1_out, not_2_out, not_3_out,
       not_4_out, or_5_out;

  not not_1 (not_1_out, B);
  not not_2 (not_2_out, C);
  not not_3 (not_3_out, D);
  not not_4 (not_4_out, E);
  and BC (BC_out, B, C);
  and BD (BD_out, B, D);
  and CD_nE (CD_nE_out, C, D, not_4_out);
  and nBDE (nBDE_out, not_1_out, D, E);
  and nBCE (nBCE_out, not_1_out, C, E);
  and B_nC_nD (B_nC_nD_out, B, not_2_out, not_3_out);
  or or_1 (Af, A, BC_out, BD_out);
  and A_nE (A_nE_out, A, not_4_out);
  or or_2 (Bf, A_nE_out, CD_nE_out, nBDE_out, nBCE_out, B_nC_nD_out);
  and B_nC_nD_2 (B_nC_nD_2_out, B, not_2_out, not_3_out);
  and C_nD_nE (C_nD_nE_out, C, not_3_out, not_4_out);
  and nC_nDE (nC_nDE_out, not_2_out, not_3_out, E);
  and CDE (CDE_out, C, D, E);
  or or_3 (Cf, A_nE_out, B_nC_nD_2_out, C_nD_nE_out, nC_nDE_out, CDE_out);
  and nDE (nDE_out, not_3_out, E);
  and nBD_nE (nBD_nE_out, not_1_out, D, not_4_out);
  and nBC_nE (nBC_nE_out, not_1_out, C, not_4_out);
  and AB (AB_out, A, B);
  and AC (AC_out, A, C);
  or or_4 (Df, B_nC_nD_2_out, nDE_out, nBD_nE_out, nBC_nE_out);
  or or_5 (or_5_out, AB_out, AC_out);
  LED ERROR (.in(or_5_out));
endmodule
